# Fritzing sketch i2c-uart-breakout_1.0 (saved by Fritzing 0.9.3b)
stripboards: 1

parts:
  J1 = female pin header, 20 pins [form="♀ (female)"]
  J2 = female pin header, 20 pins [form="♀ (female)"]
  J3 = male pin header, 4 pins [form="♂ (male)"]
  J4 = male pin header, 3 pins [form="♂ (male)"]

nets:
  N1: J1.pin5, J4.pin2
  N2: J1.pin11, J1.pin14, J3.pin3
  N3: J2.pin6, J3.pin1
  N4: J2.pin7, J3.pin4
  N5: J3.pin2, J4.pin1
