# Fritzing sketch mcp23017-sensor-array_1.0 (saved by Fritzing 0.9.3b)
stripboards: 1

parts:
  IC1 = MCP23017 I2C I/O Expander
  J1 = male pin header, 4 pins [form="♂ (male)"]
  J2 = female pin header, 4 pins [form="♀ (female)"]
  R1 = Resistor [tolerance=±5% resistance=1k package=THT]
  R2 = Resistor [tolerance=±5% resistance=2.2k package=THT]
  J3 = female pin header, 4 pins [form="♀ (female)"]
  R3 = Resistor [tolerance=±5% resistance=1k package=THT]
  R4 = Resistor [tolerance=±5% resistance=2.2k package=THT]
  J4 = female pin header, 4 pins [form="♀ (female)"]
  R5 = Resistor [tolerance=±5% resistance=1k package=THT]
  R6 = Resistor [tolerance=±5% resistance=2.2k package=THT]
  J5 = female pin header, 4 pins [form="♀ (female)"]
  R7 = Resistor [tolerance=±5% resistance=1k package=THT]
  R8 = Resistor [tolerance=±5% resistance=2.2k package=THT]
  J6 = female pin header, 4 pins [form="♀ (female)"]
  R9 = Resistor [tolerance=±5% resistance=1k package=THT]
  R10 = Resistor [tolerance=±5% resistance=2.2k package=THT]
  J7 = female pin header, 4 pins [form="♀ (female)"]
  R11 = Resistor [tolerance=±5% resistance=1k package=THT]
  R12 = Resistor [tolerance=±5% resistance=2.2k package=THT]
  J8 = female pin header, 4 pins [form="♀ (female)"]
  R13 = Resistor [tolerance=±5% resistance=1k package=THT]
  R14 = Resistor [tolerance=±5% resistance=2.2k package=THT]
  J9 = female pin header, 4 pins [form="♀ (female)"]
  R15 = Resistor [tolerance=±5% resistance=1k package=THT]
  R16 = Resistor [tolerance=±5% resistance=2.2k package=THT]
  J10 = female pin header, 4 pins [form="♀ (female)"]
  R17 = Resistor [tolerance=±5% resistance=1k package=THT]
  R18 = Resistor [tolerance=±5% resistance=2.2k package=THT]
  J11 = female pin header, 4 pins [form="♀ (female)"]
  R19 = Resistor [tolerance=±5% resistance=1k package=THT]
  R20 = Resistor [tolerance=±5% resistance=2.2k package=THT]
  J12 = female pin header, 4 pins [form="♀ (female)"]
  R21 = Resistor [tolerance=±5% resistance=2.2k package=THT]
  R22 = Resistor [tolerance=±5% resistance=1k package=THT]
  J13 = female pin header, 4 pins [form="♀ (female)"]
  R23 = Resistor [tolerance=±5% resistance=2.2k package=THT]
  R24 = Resistor [tolerance=±5% resistance=1k package=THT]
  J14 = female pin header, 4 pins [form="♀ (female)"]
  R25 = Resistor [tolerance=±5% resistance=2.2k package=THT]
  R26 = Resistor [tolerance=±5% resistance=1k package=THT]
  J15 = female pin header, 4 pins [form="♀ (female)"]
  R27 = Resistor [tolerance=±5% resistance=1k package=THT]
  R28 = Resistor [tolerance=±5% resistance=2.2k package=THT]

nets:
  N1: IC1.GPB0, J2.pin3, J3.pin3, J4.pin3, J5.pin3, J6.pin3, J7.pin3, J8.pin3
  N2: IC1.GPB1, R13.Pin_1, R14.Pin_1
  N3: IC1.GPB2, R11.Pin_1, R12.Pin_1
  N4: IC1.GPB3, R9.Pin_1, R10.Pin_1
  N5: IC1.GPB4, R5.Pin_1, R6.Pin_1
  N6: IC1.GPB5, R7.Pin_1, R8.Pin_1
  N7: IC1.GPB6, R3.Pin_1, R4.Pin_1
  N8: IC1.GPB7, R1.Pin_1, R2.Pin_1
  N9: IC1.VDD, IC1.RESET, J1.pin4, J2.pin4, J3.pin4, J4.pin4, J5.pin4, J6.pin4, J7.pin4, J8.pin4, J9.pin1, J10.pin1, J11.pin1, J12.pin1, J13.pin1, J14.pin1, J15.pin1
  N10: IC1.VSS, IC1.A0, IC1.A1, IC1.A2, J1.pin1, J2.pin1, R2.Pin_0, J3.pin1, R4.Pin_0, J4.pin1, R6.Pin_0, J5.pin1, R8.Pin_0, J6.pin1, R10.Pin_0, J7.pin1, R12.Pin_0, J8.pin1, R14.Pin_0, J9.pin4, R16.Pin_1, J10.pin4, R18.Pin_1, J11.pin4, R20.Pin_1, J12.pin4, R21.Pin_1, J13.pin4, R23.Pin_1, J14.pin4, R25.Pin_1, J15.pin4, R27.Pin_1
  N11: IC1.SCL, J1.pin2
  N12: IC1.SDA, IC1.NC#14, J1.pin3
  N13: IC1.GPA0, R15.Pin_0, R16.Pin_0
  N14: IC1.GPA1, R17.Pin_0, R18.Pin_0
  N15: IC1.GPA2, R19.Pin_0, R20.Pin_0
  N16: IC1.GPA3, R21.Pin_0, R22.Pin_0
  N17: IC1.GPA4, R23.Pin_0, R24.Pin_0
  N18: IC1.GPA5, R25.Pin_0, R26.Pin_0
  N19: IC1.GPA6, R27.Pin_0, R28.Pin_0
  N20: IC1.GPA7, J9.pin2, J10.pin2, J11.pin2, J12.pin2, J13.pin2, J14.pin2, J15.pin2
  N21: J2.pin2, R1.Pin_0
  N22: J3.pin2, R3.Pin_0
  N23: J4.pin2, R7.Pin_0
  N24: R5.Pin_0, J5.pin2
  N25: J6.pin2, R9.Pin_0
  N26: J7.pin2, R11.Pin_0
  N27: J8.pin2, R13.Pin_0
  N28: J9.pin3, R15.Pin_1
  N29: J10.pin3, R17.Pin_1
  N30: J11.pin3, R19.Pin_1
  N31: J12.pin3, R22.Pin_1
  N32: J13.pin3, R24.Pin_1
  N33: J14.pin3, R26.Pin_1
  N34: J15.pin3, R28.Pin_1

notes:
  GND
  SCL
  SCA
  V5

custom parts:
  MCP23017 I2C I/O Expander: The MCP23017 uses two i2c pins (these can be shared with other i2c devices), and in exchange gives you 16 general purpose pins. You can set each of 16 pins to be input, output, input with a pullup or open drain. There's even the ability to get an interrupt via an external pin when any of the inputs change so you don't have to keep polling the chip.
