# Fritzing sketch sensor-array_3.0 (saved by Fritzing 0.9.3b)
stripboards: 1

parts:
  J12 = female pin header, 4 pins [form="♀ (female)"]
  R18 = Resistor [tolerance=±5% resistance=2.2k package=THT]
  J13 = female pin header, 4 pins [form="♀ (female)"]
  R19 = Resistor [tolerance=±5% resistance=1k package=THT]
  R20 = Resistor [tolerance=±5% resistance=2.2k package=THT]
  J14 = female pin header, 4 pins [form="♀ (female)"]
  R21 = Resistor [tolerance=±5% resistance=1k package=THT]
  R22 = Resistor [tolerance=±5% resistance=2.2k package=THT]
  J16 = female pin header, 4 pins [form="♀ (female)"]
  R23 = Resistor [tolerance=±5% resistance=1k package=THT]  # not connected
  R24 = Resistor [tolerance=±5% resistance=2.2k package=THT]
  J18 = female pin header, 4 pins [form="♀ (female)"]
  J19 = female pin header, 4 pins [form="♀ (female)"]
  R25 = Resistor [tolerance=±5% resistance=1k package=THT]
  R26 = Resistor [tolerance=±5% resistance=2.2k package=THT]
  R27 = Resistor [tolerance=±5% resistance=1k package=THT]
  R28 = Resistor [tolerance=±5% resistance=2.2k package=THT]
  J22 = female pin header, 4 pins [form="♀ (female)"]
  R29 = Resistor [tolerance=±5% resistance=1k package=THT]
  R30 = Resistor [tolerance=±5% resistance=2.2k package=THT]
  J25 = female pin header, 4 pins [form="♀ (female)"]
  R31 = Resistor [tolerance=±5% resistance=1k package=THT]
  R32 = Resistor [tolerance=±5% resistance=2.2k package=THT]
  J27 = female pin header, 4 pins [form="♀ (female)"]
  R33 = Resistor [tolerance=±5% resistance=1k package=THT]
  R34 = Resistor [tolerance=±5% resistance=2.2k package=THT]
  J28 = female pin header, 4 pins [form="♀ (female)"]
  R35 = Resistor [tolerance=±5% resistance=1k package=THT]
  R36 = Resistor [tolerance=±5% resistance=2.2k package=THT]
  J29 = female pin header, 4 pins [form="♀ (female)"]
  R37 = Resistor [tolerance=±5% resistance=1k package=THT]
  R38 = Resistor [tolerance=±5% resistance=2.2k package=THT]
  J30 = female pin header, 4 pins [form="♀ (female)"]
  R39 = Resistor [tolerance=±5% resistance=1k package=THT]
  R40 = Resistor [tolerance=±5% resistance=2.2k package=THT]
  J31 = female pin header, 4 pins [form="♀ (female)"]
  R41 = Resistor [tolerance=±5% resistance=1k package=THT]
  R42 = Resistor [tolerance=±5% resistance=2.2k package=THT]
  J32 = female pin header, 4 pins [form="♀ (female)"]
  R43 = Resistor [tolerance=±5% resistance=1k package=THT]
  R44 = Resistor [tolerance=±5% resistance=2.2k package=THT]
  J34 = female pin header, 7 pins [form="♀ (female)"]
  J35 = female pin header, 7 pins [form="♀ (female)"]
  J15 = female pin header, 1 pin [form="♀ (female)"]
  J36 = female pin header, 2 pins [form="♀ (female)"]
  R45 = Resistor [tolerance=±5% resistance=1k package=THT]

nets:
  N1: J12.pin1, J12.pin4, R19.Pin_0, R20.Pin_0, R21.Pin_1, J16.pin2, J19.pin4, R26.Pin_0, R29.Pin_0, R29.Pin_1, J25.pin3, R33.Pin_1, R37.Pin_1, J30.pin2, R41.Pin_1, R42.Pin_1, R44.Pin_0, J34.pin7, J35.pin3, J35.pin7
  N2: J12.pin2, R18.Pin_0, J13.pin3, R22.Pin_0, J16.pin1, R24.Pin_0, J18.pin4, J19.pin1, J22.pin4, R32.Pin_1, J27.pin4, R34.Pin_0, J28.pin4, R36.Pin_0, J29.pin1, J29.pin3, J29.pin4, R37.Pin_0, R39.Pin_1, R40.Pin_1, J32.pin1, J32.pin3, J15.pin1, J36.pin1
  N3: J12.pin3, J13.pin4, R24.Pin_1, J22.pin1, R35.Pin_1, J30.pin3
  N4: J13.pin1, J14.pin3, R21.Pin_0, J18.pin3, J19.pin2, R28.Pin_1, R30.Pin_0, J25.pin4, R34.Pin_1, J28.pin3, R39.Pin_0, R42.Pin_0, R44.Pin_1, J34.pin3, J35.pin6, J36.pin2
  N5: J13.pin2, J30.pin1
  N6: J14.pin2, J29.pin2
  N7: R22.Pin_1, R31.Pin_0
  N8: R25.Pin_1, J34.pin4
  N9: R27.Pin_0, R30.Pin_1, R38.Pin_0
  N10: R27.Pin_1, J25.pin2
  N11: J27.pin2, R35.Pin_0
  N12: J27.pin3, J32.pin4
  N13: R33.Pin_0, R45.Pin_0
  N14: J28.pin1, J31.pin2, J34.pin6
  N15: J30.pin4, R43.Pin_0
  N16: R40.Pin_0, J34.pin2
  N17: J31.pin3, J35.pin1
  N18: J34.pin1, J35.pin2, R45.Pin_1
