# Fritzing sketch mcp23017-led_2.0 (saved by Fritzing 0.9.3b)
breadboards: 1

parts:
  Raspberry_Pi_1 = Raspberry Pi 3 [part_number=RPI-3-V1.2]
  IC1 = MCP23017 I2C I/O Expander
  LED3 = LED - 5mm [color="Red (633nm)" package="5 mm [THT]"]
  R4 = Resistor [tolerance=±5% resistance=1k package=THT]
  S1 = Pushbutton [package="[THT]"]
  R5 = Resistor [tolerance=±5% resistance=10k package=THT]

nets:
  5V: Raspberry_Pi_1.GPIO2, Raspberry_Pi_1.5V, IC1.VDD, IC1.SDA, IC1.RESET, S1.Pin_3, S1.Pin_4
  GND: Raspberry_Pi_1.GPIO3, Raspberry_Pi_1.GND, Raspberry_Pi_1.GPIO15, IC1.VSS, IC1.SCL, IC1.A0, IC1.A1, IC1.A2, R4.Pin_1, R5.Pin_0
  N1: IC1.GPA0, LED3.anode
  N2: IC1.GPA7, S1.Pin_1, S1.Pin_2, R5.Pin_1
  N3: LED3.cathode, R4.Pin_0

custom parts:
  MCP23017 I2C I/O Expander: The MCP23017 uses two i2c pins (these can be shared with other i2c devices), and in exchange gives you 16 general purpose pins. You can set each of 16 pins to be input, output, input with a pullup or open drain. There's even the ability to get an interrupt via an external pin when any of the inputs change so you don't have to keep polling the chip.
